# Fritzing sketch GRojFritz (saved by Fritzing 1.0.4)
breadboards: 1

parts:
  A1 = Particle - Photon2
  Part1 = BME280 Breakout  # not connected
  NEOPIXEL1 = Neopixel Strip -- Black (30/m)  # not connected
  U1 = ENCODER_RGB [package=encoder_led_2]  # not connected
  OLED_I2C1 = OLED 128x64 I2C Monochrome Display

nets:
  N1: A1.Pin_2, A1.Pin_31, OLED_I2C1.VDD
  N2: A1.Pin_4, A1.Pin_30, OLED_I2C1.GND
  N3: A1.Pin_17, OLED_I2C1.SDA
  N4: A1.Pin_18, OLED_I2C1.SCK

custom parts:
  Particle - Photon2: The Photon 2 is a microcontroller and Wi-Fi networking developed by particle. Features: 802.11a/b/g/n Wi-Fi, 2.4 GHz and 5 GHz Integrated PCB antenna Integrated U.FL connector for external antenna Integrated RF switch BLE 5 using same antenna as Wi-Fi Realtek RTL8721DM MCU ARM Cortex M33 CPU, 200 MHz 2048 KB (2 MB) user application maximum size 3072 KB (3 MB) of RAM available to user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
  Neopixel Strip -- Black (30/m): These NeoPixel strips have 30 digitally-addressable pixel LEDs per meter and are very affordable and are only 12.5 mm wide, 10 mm if you remove the strip from the casing.
  ENCODER_RGB: SparkFun RGB rotary Encoder
